// Digital circuit project05.dig as structural Verilog
module project05 (
  input  CLK,
  input  [3:0] PROG,
  input  CLR,
  output [7:0] DP,
  output [7:0] MEM,
  output [7:0] BCC,
  output [7:0] MUL,
  output [7:0] BX,
  output [7:0] ICOUNT,
  output DONE,
  output [7:0] BL,
  output [7:0] B
);

  wire and_1_out;

  and and_1 (and_1_out, CLK, ~DONE);  // And

  // Notes on the sheet:
  //   Lengend
  //   0 - quadratic-s
  //   1 - sum-array-s
  //   2 - find-max-s
  //   3 - fact-s
  //   4 - fib-rec-s
  //   5 - stolower-s
endmodule
