// Digital circuit 00_IF_DR.dig as structural Verilog
module _00_IF_DR (
  input  [31:0] IW_0,
  input  [31:0] PC4_0,
  input  [31:0] PC8_0,
  input  CLK,
  input  EN,
  input  CLR,
  output [31:0] IW_1,
  output [31:0] PC4_1,
  output [31:0] PC8_1
);

  register_clr_32bits register_clr_32bits_1 (.D(IW_0), .C(CLK), .en(EN), .Q(IW_1), .clr(CLR));
  register_clr_32bits register_clr_32bits_2 (.D(PC4_0), .C(CLK), .en(EN), .Q(PC4_1), .clr(CLR));
  register_clr_32bits register_clr_32bits_3 (.D(PC8_0), .C(CLK), .en(EN), .Q(PC8_1), .clr(CLR));
endmodule
