// Digital circuit 01_DR_EX_fwd.dig as structural Verilog
module _01_DR_EX_fwd (
  input  [31:0] IW_1,
  input  [31:0] RD0_1,
  input  [31:0] RD1_1,
  input  CLK,
  input  EN,
  input  CLR,
  input  [1:0] EXT_1,
  input  ALUB_1,
  input  [2:0] ALUO_1,
  input  MR_1,
  input  MW_1,
  input  [3:0] WR_1,
  input  WDsl_1,
  input  RFW_1,
  input  [1:0] PCsl_1,
  input  [31:0] PC4_1,
  input  [3:0] RR0_1,
  input  [3:0] RR1_1,
  output [31:0] IW_2,
  output [31:0] RD0_2,
  output [31:0] RD1_2,
  output [1:0] EXT_2,
  output ALUB_2,
  output [2:0] ALUO_2,
  output MR_2,
  output MW_2,
  output [3:0] WR_2,
  output WDsl_2,
  output RFW_2,
  output [1:0] PCsl_2,
  output [31:0] PC4_2,
  output [3:0] RR0_2,
  output [3:0] RR1_2
);

  register_clr_32bits register_clr_32bits_1 (.D(IW_1), .C(CLK), .en(EN), .Q(IW_2), .clr(CLR));
  register_clr_4bits register_clr_4bits_1 (.D(RR0_1), .C(CLK), .en(EN), .Q(RR0_2), .clr(CLR));
  register_clr_4bits register_clr_4bits_2 (.D(RR1_1), .C(CLK), .en(EN), .Q(RR1_2), .clr(CLR));
  register_clr_32bits register_clr_32bits_2 (.D(RD0_1), .C(CLK), .en(EN), .Q(RD0_2), .clr(CLR));
  register_clr_32bits register_clr_32bits_3 (.D(RD1_1), .C(CLK), .en(EN), .Q(RD1_2), .clr(CLR));
  register_clr_2bits register_clr_2bits_1 (.D(EXT_1), .C(CLK), .en(EN), .Q(EXT_2), .clr(CLR));
  register_clr_1bit register_clr_1bit_1 (.D(ALUB_1), .C(CLK), .en(EN), .Q(ALUB_2), .clr(CLR));
  register_clr_3bits register_clr_3bits_1 (.D(ALUO_1), .C(CLK), .en(EN), .Q(ALUO_2), .clr(CLR));
  register_clr_1bit register_clr_1bit_2 (.D(MR_1), .C(CLK), .en(EN), .Q(MR_2), .clr(CLR));
  register_clr_1bit register_clr_1bit_3 (.D(MW_1), .C(CLK), .en(EN), .Q(MW_2), .clr(CLR));
  register_clr_4bits register_clr_4bits_3 (.D(WR_1), .C(CLK), .en(EN), .Q(WR_2), .clr(CLR));
  register_clr_1bit register_clr_1bit_4 (.D(WDsl_1), .C(CLK), .en(EN), .Q(WDsl_2), .clr(CLR));
  register_clr_1bit register_clr_1bit_5 (.D(RFW_1), .C(CLK), .en(EN), .Q(RFW_2), .clr(CLR));
  register_clr_2bits register_clr_2bits_2 (.D(PCsl_1), .C(CLK), .en(EN), .Q(PCsl_2), .clr(CLR));
  register_clr_32bits register_clr_32bits_4 (.D(PC4_1), .C(CLK), .en(EN), .Q(PC4_2), .clr(CLR));
endmodule
