// Digital circuit 02_EX_MEM.dig as structural Verilog
module _02_EX_MEM (
  input  [31:0] IW_2,
  input  [31:0] ALUR_2,
  input  [31:0] RD1_2,
  input  CLK,
  input  EN,
  input  CLR,
  input  MR_2,
  input  MW_2,
  input  [3:0] WR_2,
  input  WDsl_2,
  input  RFW_2,
  input  [1:0] PCsl_2,
  input  [31:0] PC4_2,
  output [31:0] IW_3,
  output [31:0] ALUR_3,
  output [31:0] RD1_3,
  output MR_3,
  output MW_3,
  output [3:0] WR_3,
  output WDsl_3,
  output RFW_3,
  output [1:0] PCsl_3,
  output [31:0] PC4_3
);

  register_clr_32bits register_clr_32bits_1 (.D(IW_2), .C(CLK), .en(EN), .Q(IW_3), .clr(CLR));
  register_clr_32bits register_clr_32bits_2 (.D(ALUR_2), .C(CLK), .en(EN), .Q(ALUR_3), .clr(CLR));
  register_clr_32bits register_clr_32bits_3 (.D(RD1_2), .C(CLK), .en(EN), .Q(RD1_3), .clr(CLR));
  register_clr_1bit register_clr_1bit_1 (.D(MR_2), .C(CLK), .en(EN), .Q(MR_3), .clr(CLR));
  register_clr_1bit register_clr_1bit_2 (.D(MW_2), .C(CLK), .en(EN), .Q(MW_3), .clr(CLR));
  register_clr_4bits register_clr_4bits_1 (.D(WR_2), .C(CLK), .en(EN), .Q(WR_3), .clr(CLR));
  register_clr_1bit register_clr_1bit_3 (.D(WDsl_2), .C(CLK), .en(EN), .Q(WDsl_3), .clr(CLR));
  register_clr_1bit register_clr_1bit_4 (.D(RFW_2), .C(CLK), .en(EN), .Q(RFW_3), .clr(CLR));
  register_clr_2bits register_clr_2bits_1 (.D(PCsl_2), .C(CLK), .en(EN), .Q(PCsl_3), .clr(CLR));
  register_clr_32bits register_clr_32bits_4 (.D(PC4_2), .C(CLK), .en(EN), .Q(PC4_3), .clr(CLR));
endmodule
