// Digital circuit 03_MEM_WB.dig as structural Verilog
module _03_MEM_WB (
  input  [31:0] IW_3,
  input  [31:0] ALUR_3,
  input  [31:0] MRD_3,
  input  CLK,
  input  EN,
  input  CLR,
  input  MR_3,
  input  [3:0] WR_3,
  input  WDsl_3,
  input  RFW_3,
  input  [1:0] PCsl_3,
  input  [31:0] PC4_3,
  output [31:0] IW_4,
  output [31:0] ALUR_4,
  output [31:0] MRD_4,
  output MR_4,
  output [3:0] WR_4,
  output WDsl_4,
  output RFW_4,
  output [1:0] PCsl_4,
  output [31:0] PC4_4
);

  register_clr_32bits register_clr_32bits_1 (.D(IW_3), .C(CLK), .en(EN), .Q(IW_4), .clr(CLR));
  register_clr_32bits register_clr_32bits_2 (.D(ALUR_3), .C(CLK), .en(EN), .Q(ALUR_4), .clr(CLR));
  register_clr_32bits register_clr_32bits_3 (.D(MRD_3), .C(CLK), .en(EN), .Q(MRD_4), .clr(CLR));
  register_clr_1bit register_clr_1bit_1 (.D(MR_3), .C(CLK), .en(EN), .Q(MR_4), .clr(CLR));
  register_clr_4bits register_clr_4bits_1 (.D(WR_3), .C(CLK), .en(EN), .Q(WR_4), .clr(CLR));
  register_clr_1bit register_clr_1bit_2 (.D(WDsl_3), .C(CLK), .en(EN), .Q(WDsl_4), .clr(CLR));
  register_clr_1bit register_clr_1bit_3 (.D(RFW_3), .C(CLK), .en(EN), .Q(RFW_4), .clr(CLR));
  register_clr_2bits register_clr_2bits_1 (.D(PCsl_3), .C(CLK), .en(EN), .Q(PCsl_4), .clr(CLR));
  register_clr_32bits register_clr_32bits_4 (.D(PC4_3), .C(CLK), .en(EN), .Q(PC4_4), .clr(CLR));
endmodule
