// Digital circuit 4to16_decoder_with_enable.dig as structural Verilog
module _4to16_decoder_with_enable (
  input  [3:0] Sel,
  input  EN,
  output out_0,
  output out_1,
  output out_2,
  output out_3,
  output out_4,
  output out_5,
  output out_6,
  output out_7,
  output out_8,
  output out_9,
  output out_10,
  output out_11,
  output out_12,
  output out_13,
  output out_14,
  output out_15
);

  wire decoder_1_out_0, decoder_1_out_1, decoder_1_out_2, decoder_1_out_3, decoder_1_out_4, decoder_1_out_5,
       decoder_1_out_6, decoder_1_out_7, decoder_1_out_8, decoder_1_out_9, decoder_1_out_10,
       decoder_1_out_11, decoder_1_out_12, decoder_1_out_13, decoder_1_out_14, decoder_1_out_15;

  Decoder #(.Selector_Bits(4)) decoder_1 (
    .sel(Sel), .out_0(decoder_1_out_0), .out_1(decoder_1_out_1), .out_2(decoder_1_out_2),
    .out_3(decoder_1_out_3), .out_4(decoder_1_out_4), .out_5(decoder_1_out_5), .out_6(decoder_1_out_6),
    .out_7(decoder_1_out_7), .out_8(decoder_1_out_8), .out_9(decoder_1_out_9), .out_10(decoder_1_out_10),
    .out_11(decoder_1_out_11), .out_12(decoder_1_out_12), .out_13(decoder_1_out_13),
    .out_14(decoder_1_out_14), .out_15(decoder_1_out_15));
  and and_1 (out_0, decoder_1_out_0, EN);
  and and_2 (out_1, decoder_1_out_1, EN);
  and and_3 (out_2, decoder_1_out_2, EN);
  and and_4 (out_3, decoder_1_out_3, EN);
  and and_5 (out_4, decoder_1_out_4, EN);
  and and_6 (out_5, decoder_1_out_5, EN);
  and and_7 (out_6, decoder_1_out_6, EN);
  and and_8 (out_7, decoder_1_out_7, EN);
  and and_9 (out_8, decoder_1_out_8, EN);
  and and_10 (out_9, decoder_1_out_9, EN);
  and and_11 (out_10, decoder_1_out_10, EN);
  and and_12 (out_11, decoder_1_out_11, EN);
  and and_13 (out_12, decoder_1_out_12, EN);
  and and_14 (out_13, decoder_1_out_13, EN);
  and and_15 (out_14, decoder_1_out_14, EN);
  and and_16 (out_15, decoder_1_out_15, EN);
endmodule
