// Digital circuit alu.dig as structural Verilog
module alu (
  input  [31:0] A,
  input  [31:0] B,
  input  [2:0] ALUOp,
  output [31:0] R,
  output [3:0] NZCV,
  output N,
  output Z,
  output C,
  output V
);

  wire [31:0] add_1_s, sub_1_s;
  wire [63:0] mul_1_mul;

  Comparator #(.Bits(32)) Zero (.a({N, R[30:0]}), .b({32{1'b0}}), .eq(NZCV[1]));  // open: gt, lt
  Comparator #(.Bits(32)) Carry (.a(B), .b(A), .gt(C));  // open: eq, lt
  Add #(.Bits(32)) add_1 (.a(A), .b(B), .c_i(1'b0), .s(add_1_s));  // open: c_o
  Sub #(.Bits(32)) sub_1 (.a(A), .b(B), .c_i(1'b0), .s(sub_1_s));  // open: c_o
  Mul #(.Bits(32)) mul_1 (.a(A), .b(B), .mul(mul_1_mul));
  Multiplexer #(.Selector_Bits(3), .Bits(32)) multiplexer_1 (
    .sel(ALUOp), .in_0(add_1_s), .in_1(sub_1_s), .in_2(mul_1_mul[31:0]), .in_3(B), .in_4({32{1'b0}}),
    .in_5({32{1'b0}}), .in_6({32{1'b0}}), .in_7({32{1'b0}}), .out({N, R[30:0]}));

  assign {NZCV[3:2], NZCV[0]} = {1'b0, C, N};
  assign R[31] = N;
  assign V = 1'b0;
  assign Z = NZCV[1];
endmodule
