// Digital circuit control_unit.dig as structural Verilog
module control_unit (
  input  [31:0] iw,
  output RFW,
  output [1:0] EXT,
  output [1:0] ALUop,
  output BR,
  output ALU1src
);

  wire and_1_out, and_2_out, and_3_out, comparator_1_eq, comparator_2_eq;

  // Probe on iw
  Comparator #(.Bits(4)) comparator_1 (.a(iw[24:21]), .b(4'b0100), .eq(comparator_1_eq));  // open: gt, lt
  Comparator #(.Bits(4)) comparator_2 (.a(iw[24:21]), .b(4'b1101), .eq(comparator_2_eq));  // open: gt, lt
  and and_1 (and_1_out, ~iw[27], ~iw[26], ~iw[25], comparator_1_eq);  // And
  and and_2 (and_2_out, ~iw[27], ~iw[26], iw[25], comparator_2_eq);  // And
  and and_3 (and_3_out, iw[27], ~iw[26], iw[25]);  // And
  or or_1 (RFW, and_1_out, and_2_out);
  or or_2 (EXT[0], 1'b0, 1'b0);
  or or_3 (EXT[1], and_3_out, 1'b0);
  or or_4 (ALUop[0], and_2_out, 1'b0);
  or or_5 (ALUop[1], and_2_out, 1'b0);
  or or_6 (ALU1src, and_2_out, and_3_out);
  or or_7 (BR, and_3_out, 1'b0);

  // Other names for the same wires on the sheet: b_offset[23:0] = iw[23:0]; imm[7:0] = iw[7:0];
  //   immoff[11:0] = iw[11:0]; rm[3:0] = iw[3:0]; rm_mul[3:0] = iw[3:0]; opmul4[3:0] = iw[7:4];
  //   rs_mul[3:0] = iw[11:8]; rd[3:0] = iw[15:12]; rn_mul[3:0] = iw[15:12]; rd_mul[3:0] = iw[19:16];
  //   rn[3:0] = iw[19:16]; l_sdt = iw[20]; s_dp = iw[20]; s_mul = iw[20]; a_mul = iw[21]; opc[3:0] = iw[24:21];
  //   w_sdt = iw[21]; b_sdt = iw[22]; opmul6[4:0] = iw[27:23]; u_sdt = iw[23]; l_b = iw[24]; p_sdt = iw[24];
  //   i_sdt = iw[25]; op0 = iw[25]; op0_i_dp = iw[25]; op1 = iw[26]; opmul2[1:0] = iw[27:26]; op2 = iw[27];
  //   cond[3:0] = iw[31:28]

  // Notes on the sheet:
  //   addr
  //   movi
  //   b
endmodule
