// Digital circuit decode_ascii.dig as structural Verilog
module decode_ascii (
  input  [31:0] IW,
  output [7:0] I_0,
  output [7:0] I_1,
  output [7:0] I_2,
  output [7:0] I_3
);

  wire [3:0] decoder_inum_1_inum;

  decoder_inum decoder_inum_1 (.IW(IW), .INUM(decoder_inum_1_inum));
  ROM #(.AddrBits(4), .Bits(32)) rom_1 (.A(decoder_inum_1_inum), .sel(1'b1), .D({I_0, I_1, I_2, I_3}));
  // Probe on I_0
  // Probe on I_1
  // Probe on I_2
  // Probe on I_3

  // Notes on the sheet:
  //   contents of rom_1 (hex, n*v repeats v):
  //   41444452,41444449,4d4f5652,4d4f5649,4c445249,53545249,425f5f5f
  //   ,424c5f5f,42585f5f,4e4f505f,4e4f4e45
endmodule
