// Digital circuit decoder.dig as structural Verilog
module decoder (
  input  [31:0] IW,
  output RFW,
  output [1:0] EXTop,
  output ALUsrcB,
  output [2:0] ALUop,
  output [1:0] PCsel,
  output [1:0] RR0sel,
  output RR1sel,
  output WRsel,
  output WDsel,
  output MR,
  output MW
);

  wire [3:0] decoder_inum_1_inum;

  decoder_inum decoder_inum_1 (.IW(IW), .INUM(decoder_inum_1_inum));
  ROM #(.AddrBits(4), .Bits(16)) rom_1 (
    .A(decoder_inum_1_inum), .sel(1'b1),
    .D({RFW, EXTop, ALUsrcB, ALUop, PCsel, RR0sel, RR1sel, WRsel, WDsel, MR, MW}));
  // Probe on RFW
  // Probe on EXTop
  // Probe on ALUsrcB
  // Probe on ALUop
  // Probe on PCsel
  // Probe on RR0sel
  // Probe on RR1sel
  // Probe on WRsel
  // Probe on WDsel
  // Probe on MR
  // Probe on MW

  // Notes on the sheet:
  //   contents of rom_1 (hex, n*v repeats v):
  //   8000,9000,8600,9600,b002,3011,50a0,d0ac,100
endmodule
