// Digital circuit decoder_inum.dig as structural Verilog
module decoder_inum (
  input  [31:0] IW,
  output [3:0] INUM
);

  wire add_i_eq, add_r_eq, b_eq, bl_eq, bx_eq, ldr_i_eq, mov_i_eq, mov_r_eq, none_eq, nop_eq, str_i_eq;

  // Probe on IW[27:20]
  // Probe on IW[27:24]
  // Probe on IW[27:4]
  Comparator #(.Bits(8)) add_r (.a(IW[27:20]), .b(8'h8), .eq(add_r_eq));  // open: gt, lt
  Comparator #(.Bits(8)) add_i (.a(IW[27:20]), .b(8'h28), .eq(add_i_eq));  // open: gt, lt
  Comparator #(.Bits(8)) mov_r (.a(IW[27:20]), .b(8'h1a), .eq(mov_r_eq));  // open: gt, lt
  Comparator #(.Bits(8)) mov_i (.a(IW[27:20]), .b(8'h3a), .eq(mov_i_eq));  // open: gt, lt
  Comparator #(.Bits(8)) ldr_i (.a(IW[27:20]), .b(8'h59), .eq(ldr_i_eq));  // open: gt, lt
  Comparator #(.Bits(8)) str_i (.a(IW[27:20]), .b(8'h58), .eq(str_i_eq));  // open: gt, lt
  Comparator #(.Bits(4)) b (.a(IW[27:24]), .b(4'b1010), .eq(b_eq));  // open: gt, lt
  Comparator #(.Bits(4)) bl (.a(IW[27:24]), .b(4'b1011), .eq(bl_eq));  // open: gt, lt
  Comparator #(.Bits(24)) bx (.a(IW[27:4]), .b(24'h12fff1), .eq(bx_eq));  // open: gt, lt
  Comparator #(.Bits(32)) nop (.a(IW), .b(32'he1a00000), .eq(nop_eq));  // open: gt, lt
  Comparator #(.Bits(32)) none (.a(IW), .b({32{1'b0}}), .eq(none_eq));  // open: gt, lt
  PriorityEncoder #(.Selector_Bits(4)) Output_Bits (
    .in0(add_r_eq), .in1(add_i_eq), .in2(mov_r_eq), .in3(mov_i_eq), .in4(ldr_i_eq), .in5(str_i_eq),
    .in6(b_eq), .in7(bl_eq), .in8(bx_eq), .in9(nop_eq), .in10(none_eq), .in11(1'b0), .in12(1'b0),
    .in13(1'b0), .in14(1'b0), .in15(1'b0), .num(INUM));  // open: any

  // Other names for the same wires on the sheet: bits27_4[23:0] = IW[27:4]; bits27_20[7:0] = IW[27:20];
  //   bits27_24[3:0] = IW[27:24]
endmodule
