// Digital circuit extension_unit.dig as structural Verilog
module extension_unit (
  input  [31:0] iw,
  input  [1:0] EXT,
  output [31:0] extimm
);

  wire [31:0] barrelshifter_1_out, bitextender_1_out;

  BitExtender #(.inputBits(24), .outputBits(32)) bitextender_1 (.in(iw[23:0]), .out(bitextender_1_out));
  BarrelShifter #(.Bits(32)) barrelshifter_1 (.in(bitextender_1_out), .shift(6'b000010), .out(barrelshifter_1_out));
  Multiplexer #(.Selector_Bits(2), .Bits(32)) multiplexer_1 (
    .sel(EXT), .in_0({{24{1'b0}}, iw[7:0]}), .in_1({{20{1'b0}}, iw[11:0]}), .in_2(barrelshifter_1_out),
    .in_3({32{1'b0}}), .out(extimm));
  // Pins of 1 and 32 bits meet at extimm
endmodule
