// Digital circuit instruction_memory.dig as structural Verilog
module instruction_memory (
  input  [6:0] A,
  input  [2:0] PN,
  output [31:0] D
);

  wire [31:0] _00_dp_3nop_d, _01_dp_2nop_d, _02_blbx_d, _03_ldr_d, _04_dp_fwd_d, _05_ldr_stl_d,
       _06_blbx_fls_d;

  ROM #(.AddrBits(7), .Bits(32)) _00_dp_3nop (.A(A), .sel(1'b1), .D(_00_dp_3nop_d));
  ROM #(.AddrBits(7), .Bits(32)) _01_dp_2nop (.A(A), .sel(1'b1), .D(_01_dp_2nop_d));
  ROM #(.AddrBits(7), .Bits(32)) _02_blbx (.A(A), .sel(1'b1), .D(_02_blbx_d));
  ROM #(.AddrBits(7), .Bits(32)) _03_ldr (.A(A), .sel(1'b1), .D(_03_ldr_d));
  ROM #(.AddrBits(7), .Bits(32)) _04_dp_fwd (.A(A), .sel(1'b1), .D(_04_dp_fwd_d));
  ROM #(.AddrBits(7), .Bits(32)) _05_ldr_stl (.A(A), .sel(1'b1), .D(_05_ldr_stl_d));
  ROM #(.AddrBits(7), .Bits(32)) _06_blbx_fls (.A(A), .sel(1'b1), .D(_06_blbx_fls_d));
  Multiplexer #(.Selector_Bits(3), .Bits(32)) multiplexer_1 (
    .sel(PN), .in_0(_00_dp_3nop_d), .in_1(_01_dp_2nop_d), .in_2(_02_blbx_d), .in_3(_03_ldr_d),
    .in_4(_04_dp_fwd_d), .in_5(_05_ldr_stl_d), .in_6(_06_blbx_fls_d), .in_7({32{1'b0}}), .out(D));

  // Notes on the sheet:
  //   contents of _00_dp_3nop (hex, n*v repeats v):
  //   e3a01001,e1a00000,e1a00000,e1a00000,e3a02002,e1a00000,e1a00000,e1a00000,e0810002,
  //   e1a00000,e1a00000,e1a00000,e2800001,e1a00000,e1a00000,e1a00000,e2800000,e1a00000,
  //   e1a00000,e1a00000,e1a00000
  //   contents of _01_dp_2nop (hex, n*v repeats v):
  //   e3a01001,e1a00000,e1a00000,e3a02002,e1a00000,e1a00000,e0810002,e1a00000,e1a00000,
  //   e2800001,e1a00000,e1a00000,e2800000,e1a00000,e1a00000,e1a00000,e1a00000
  //   contents of _02_blbx (hex, n*v repeats v):
  //   e3a01001,e1a00000,e1a00000,e3a02002,e1a00000,e1a00000,eb000008,e1a00000,e1a00000,
  //   e1a00000,e1a00000,e2800000,e1a00000,e1a00000,e1a00000,e1a00000,e0810002,e1a00000,
  //   e1a00000,e2800001,e1a00000,e1a00000,e12fff1e,e1a00000,e1a00000,e1a00000,e1a00000
  //   contents of _03_ldr (hex, n*v repeats v):
  //   e3a01001,e3a02002,e0810002,e2800001,e3a03000,e3a04063,e5834000,e5935000,e2850001,
  //   e2800000,e1a00000,e1a00000,e1a00000,e1a00000
  //   contents of _04_dp_fwd (hex, n*v repeats v):
  //   e3a01001,e3a02002,e0810002,e2800000
  //   contents of _05_ldr_stl (hex, n*v repeats v):
  //   e3a00000,e3a01001,e5801000,e5902000,e2820001,e2800000
  //   contents of _06_blbx_fls (hex, n*v repeats v):
  //   e3a00002,eb000000,e2800000,e2800004,e12fff1e
endmodule
