// Digital circuit project07_pipelined.dig as structural Verilog
module project07_pipelined (
  input  CLK,
  input  CLR,
  input  [2:0] PROG,
  output DONE,
  output [31:0] R0
);

  wire a_mul, ALUB_1, ALUB_2, C, CLK_t, i_dp, MR_1, MR_2, MR_3, MR_4, MW_1, MW_2, MW_3, N, not_1_out, RFW_1,
       RFW_2, RFW_3, RFW_4, RR1sl_1, V, WDsl_1, WDsl_2, WDsl_3, WDsl_4, WRsl_1, Z;
  wire [1:0] EXT_1, EXT_2, PCsl_1, PCsl_2, PCsl_3, PCsl_4, RR0sl_1;
  wire [2:0] ALUO_1, ALUO_2;
  wire [3:0] cond, multiplexer_2_out, multiplexer_3_out, WR_1, WR_2, WR_3, WR_4;
  wire [7:0] decode_ascii_1_i_0, decode_ascii_1_i_1, decode_ascii_1_i_2, decode_ascii_1_i_3,
       decode_ascii_2_i_0, decode_ascii_2_i_1, decode_ascii_2_i_2, decode_ascii_2_i_3, decode_ascii_3_i_0,
       decode_ascii_3_i_1, decode_ascii_3_i_2, decode_ascii_3_i_3, decode_ascii_4_i_0, decode_ascii_4_i_1,
       decode_ascii_4_i_2, decode_ascii_4_i_3, decode_ascii_5_i_0, decode_ascii_5_i_1, decode_ascii_5_i_2,
       decode_ascii_5_i_3;
  wire [23:0] b_offset;
  wire [27:24] IW_0;
  wire [31:0] _00_if_dr_1_pc4_1, _00_if_dr_1_pc8_1, _01_dr_ex_1_rd0_2, _01_dr_ex_1_rd1_2,
       _02_ex_mem_1_alur_3, _02_ex_mem_1_rd1_3, _03_mem_wb_1_alur_4, _03_mem_wb_1_mrd_4, _03_mem_wb_1_pc4_4,
       add_1_s, add_2_s, alu_1_r, extension_unit_1_p3, IW_1, IW_2, IW_3, IW_4, multiplexer_1_out,
       multiplexer_5_out, multiplexer_6_out, multiplexer_7_out, PC4_2, PC4_3, r1, r2, r3, r4, r5, r6, r7, r8,
       r9, r10, r11, r12, r13, r14, r15, RAM_d, register_clr_32bits_1_q, register_file_clr_1_rd0,
       register_file_clr_1_rd1;

  // Probe on {cond, IW_0[27:26], i_dp, IW_0[24], b_offset[23:22], a_mul, b_offset[20:0]}
  and and_1 (CLK_t, CLK, ~DONE);  // And
  register_clr_32bits register_clr_32bits_1 (
    .D(multiplexer_1_out), .C(CLK_t), .en(1'b1), .Q(register_clr_32bits_1_q), .clr(CLR));
  Multiplexer #(.Selector_Bits(2), .Bits(32)) multiplexer_1 (
    .sel(PCsl_4), .in_0(add_1_s), .in_1(multiplexer_7_out), .in_2(_01_dr_ex_1_rd1_2), .in_3({32{1'b0}}),
    .out(multiplexer_1_out));
  // Probe on decode_ascii_1_i_0
  // Probe on decode_ascii_1_i_1
  decode_ascii decode_ascii_1 (
    .IW({cond, IW_0[27:26], i_dp, IW_0[24], b_offset[23:22], a_mul, b_offset[20:0]}),
    .I_0(decode_ascii_1_i_0), .I_1(decode_ascii_1_i_1), .I_2(decode_ascii_1_i_2), .I_3(decode_ascii_1_i_3));
  Add #(.Bits(32)) add_1 (.a(register_clr_32bits_1_q), .b(32'h4), .c_i(1'b0), .s(add_1_s));  // open: c_o
  // Probe on decode_ascii_1_i_2
  // Probe on decode_ascii_1_i_3
  instruction_memory instruction_memory_1 (
    .A(register_clr_32bits_1_q[8:2]), .PN(PROG),
    .D({cond, IW_0[27:26], i_dp, IW_0[24], b_offset[23:22], a_mul, b_offset[20:0]}));
  Add #(.Bits(32)) add_2 (.a(add_1_s), .b(32'h4), .c_i(1'b0), .s(add_2_s));  // open: c_o
  // Probe on R0
  // Probe on r1
  // Probe on r2
  // Probe on r3
  // Probe on cond
  // Probe on cond
  // Probe on cond
  // Probe on cond
  _00_IF_DR _00_if_dr_1 (
    .IW_0({cond, IW_0[27:26], i_dp, IW_0[24], b_offset[23:22], a_mul, b_offset[20:0]}), .PC4_0(add_1_s),
    .PC8_0(add_2_s), .IW_1(IW_1), .PC4_1(_00_if_dr_1_pc4_1), .PC8_1(_00_if_dr_1_pc8_1), .CLK(CLK_t),
    .EN(1'b1), .CLR(CLR));
  // Probe on r4
  // Probe on r5
  // Probe on r6
  // Probe on r7
  // Probe on IW_0[27:26]
  // Probe on {IW_0[27:26], i_dp, IW_0[24], b_offset[23]}
  // Probe on IW_0[27:26]
  // Probe on {IW_0[27:26], i_dp}
  // Probe on i_dp
  // Probe on i_dp
  // Probe on IW_0[24]
  decode_ascii decode_ascii_2 (
    .IW(IW_1), .I_0(decode_ascii_2_i_0), .I_1(decode_ascii_2_i_1), .I_2(decode_ascii_2_i_2),
    .I_3(decode_ascii_2_i_3));
  // Probe on {IW_0[24], b_offset[23:22], a_mul}
  // Probe on a_mul
  // Probe on IW_0[24]
  // Probe on decode_ascii_2_i_0
  // Probe on decode_ascii_2_i_1
  // Probe on r8
  // Probe on r9
  // Probe on r10
  // Probe on r11
  // Probe on b_offset[20]
  // Probe on b_offset[23]
  // Probe on {b_offset[23:22], a_mul, b_offset[20:0]}
  Multiplexer #(.Selector_Bits(2), .Bits(4)) multiplexer_2 (
    .sel(RR0sl_1), .in_0(IW_1[19:16]), .in_1(4'b1111), .in_2(4'b0000), .in_3(4'b0000), .out(multiplexer_2_out));
  Multiplexer #(.Bits(4)) multiplexer_3 (.sel(RR1sl_1), .in_0(IW_1[3:0]), .in_1(IW_1[15:12]), .out(multiplexer_3_out));
  Multiplexer #(.Bits(4)) multiplexer_4 (.sel(WRsl_1), .in_0(IW_1[15:12]), .in_1(4'b1110), .out(WR_1));
  Multiplexer #(.Bits(32)) multiplexer_5 (
    .sel(WDsl_4), .in_0(multiplexer_7_out), .in_1(_03_mem_wb_1_pc4_4), .out(multiplexer_5_out));
  // Probe on decode_ascii_2_i_2
  // Probe on decode_ascii_2_i_3
  // Probe on b_offset[20]
  // Probe on b_offset[19:16]
  // Probe on b_offset[22]
  decoder decoder_1 (
    .IW(IW_1), .RFW(RFW_1), .EXTop(EXT_1), .ALUsrcB(ALUB_1), .ALUop(ALUO_1), .PCsel(PCsl_1),
    .RR0sel(RR0sl_1), .RR1sel(RR1sl_1), .WRsel(WRsl_1), .WDsel(WDsl_1), .MR(MR_1), .MW(MW_1));
  not not_1 (not_1_out, CLK_t);
  // Probe on b_offset[19:16]
  // Probe on b_offset[15:12]
  // Probe on a_mul
  register_file_clr register_file_clr_1 (
    .ReadReg0(multiplexer_2_out), .ReadReg1(multiplexer_3_out), .WriteReg(WR_4),
    .WriteData(multiplexer_5_out), .WriteEn(RFW_4), .PC(_00_if_dr_1_pc8_1), .CLK(not_1_out),
    .RD0(register_file_clr_1_rd0), .RD1(register_file_clr_1_rd1), .r0(R0), .r1(r1), .r2(r2), .r3(r3),
    .r4(r4), .r5(r5), .r6(r6), .r7(r7), .r8(r8), .r9(r9), .r10(r10), .r11(r11), .r12(r12), .r13(r13),
    .r14(r14), .r15(r15), .CLR(CLR));
  // Probe on r12
  // Probe on r13
  // Probe on r14
  // Probe on r15
  // Probe on b_offset[15:12]
  // Probe on b_offset[11:8]
  // Probe on b_offset[20]
  // Probe on b_offset[3:0]
  // Probe on b_offset[7:0]
  // Probe on b_offset[19:16]
  // Probe on N
  // Probe on Z
  // Probe on C
  // Probe on V
  // Probe on b_offset[7:4]
  // Probe on b_offset[15:12]
  // Probe on b_offset[3:0]
  // Probe on b_offset[3:0]
  // Probe on b_offset[11:0]
  _01_DR_EX _01_dr_ex_1 (
    .IW_1(IW_1), .RD0_1(register_file_clr_1_rd0), .RD1_1(register_file_clr_1_rd1), .EXT_1(EXT_1),
    .ALUB_1(ALUB_1), .ALUO_1(ALUO_1), .MR_1(MR_1), .MW_1(MW_1), .WR_1(WR_1), .WDsl_1(WDsl_1), .RFW_1(RFW_1),
    .PCsl_1(PCsl_1), .PC4_1(_00_if_dr_1_pc4_1), .IW_2(IW_2), .RD0_2(_01_dr_ex_1_rd0_2),
    .RD1_2(_01_dr_ex_1_rd1_2), .EXT_2(EXT_2), .ALUB_2(ALUB_2), .ALUO_2(ALUO_2), .MR_2(MR_2), .MW_2(MW_2),
    .WR_2(WR_2), .WDsl_2(WDsl_2), .RFW_2(RFW_2), .PCsl_2(PCsl_2), .PC4_2(PC4_2), .CLK(CLK_t), .EN(1'b1),
    .CLR(CLR));
  Comparator #(.Bits(32)) comparator_1 (.a(IW_4), .b(32'he2800000), .eq(DONE));  // open: gt, lt
  // Probe on decode_ascii_3_i_0
  decode_ascii decode_ascii_3 (
    .IW(IW_2), .I_0(decode_ascii_3_i_0), .I_1(decode_ascii_3_i_1), .I_2(decode_ascii_3_i_2),
    .I_3(decode_ascii_3_i_3));
  // Probe on decode_ascii_3_i_1
  // Probe on decode_ascii_3_i_2
  Multiplexer #(.Bits(32)) multiplexer_6 (
    .sel(ALUB_2), .in_0(_01_dr_ex_1_rd1_2), .in_1(extension_unit_1_p3), .out(multiplexer_6_out));
  // extension_unit extension_unit_1: pin names not known; wires that end beside it: IW_2, EXT_2, extension_unit_1_p3
  // Probe on decode_ascii_3_i_3
  alu alu_1 (
    .A(_01_dr_ex_1_rd0_2), .B(multiplexer_6_out), .R(alu_1_r), .N(N), .Z(Z), .C(C), .V(V), .ALUOp(ALUO_2));  // open: NZCV
  // Probe on extension_unit_1_p3
  _02_EX_MEM _02_ex_mem_1 (
    .IW_2(IW_2), .ALUR_2(alu_1_r), .RD1_2(_01_dr_ex_1_rd1_2), .MR_2(MR_2), .MW_2(MW_2), .WR_2(WR_2),
    .WDsl_2(WDsl_2), .RFW_2(RFW_2), .PCsl_2(PCsl_2), .PC4_2(PC4_2), .IW_3(IW_3),
    .ALUR_3(_02_ex_mem_1_alur_3), .RD1_3(_02_ex_mem_1_rd1_3), .MR_3(MR_3), .MW_3(MW_3), .WR_3(WR_3),
    .WDsl_3(WDsl_3), .RFW_3(RFW_3), .PCsl_3(PCsl_3), .PC4_3(PC4_3), .CLK(CLK_t), .EN(1'b1), .CLR(CLR));
  decode_ascii decode_ascii_4 (
    .IW(IW_3), .I_0(decode_ascii_4_i_0), .I_1(decode_ascii_4_i_1), .I_2(decode_ascii_4_i_2),
    .I_3(decode_ascii_4_i_3));
  // Probe on decode_ascii_4_i_0
  // Probe on decode_ascii_4_i_1
  RAMDualPort #(.AddrBits(8), .Bits(32)) RAM (
    .A(_02_ex_mem_1_alur_3[9:2]), .Din(_02_ex_mem_1_rd1_3), .str(MW_3), .C(CLK_t), .ld(MR_3), .D(RAM_d));
  // Probe on decode_ascii_4_i_2
  // Probe on decode_ascii_4_i_3
  _03_MEM_WB _03_mem_wb_1 (
    .IW_3(IW_3), .ALUR_3(_02_ex_mem_1_alur_3), .MRD_3(RAM_d), .MR_3(MR_3), .WR_3(WR_3), .WDsl_3(WDsl_3),
    .RFW_3(RFW_3), .PCsl_3(PCsl_3), .PC4_3(PC4_3), .IW_4(IW_4), .ALUR_4(_03_mem_wb_1_alur_4),
    .MRD_4(_03_mem_wb_1_mrd_4), .MR_4(MR_4), .WR_4(WR_4), .WDsl_4(WDsl_4), .RFW_4(RFW_4), .PCsl_4(PCsl_4),
    .PC4_4(_03_mem_wb_1_pc4_4), .CLK(CLK_t), .EN(1'b1), .CLR(CLR));
  // Probe on decode_ascii_5_i_0
  decode_ascii decode_ascii_5 (
    .IW(IW_4), .I_0(decode_ascii_5_i_0), .I_1(decode_ascii_5_i_1), .I_2(decode_ascii_5_i_2),
    .I_3(decode_ascii_5_i_3));
  Multiplexer #(.Bits(32)) multiplexer_7 (
    .sel(MR_4), .in_0(_03_mem_wb_1_alur_4), .in_1(_03_mem_wb_1_mrd_4), .out(multiplexer_7_out));
  // Probe on decode_ascii_5_i_1
  // Probe on decode_ascii_5_i_2
  // Probe on decode_ascii_5_i_3

  // Other names for the same wires on the sheet: imm[7:0] = b_offset[7:0]; immoff[11:0] = b_offset[11:0];
  //   IW_0 (some bits) = {cond, i_dp, b_offset[23:22], a_mul, b_offset[20:0]}; rm[3:0] = b_offset[3:0];
  //   rm_mul[3:0] = b_offset[3:0]; opmul4[3:0] = b_offset[7:4]; rs_mul[3:0] = b_offset[11:8];
  //   rd[3:0] = b_offset[15:12]; rn_mul[3:0] = b_offset[15:12]; rd_mul[3:0] = b_offset[19:16];
  //   rn[3:0] = b_offset[19:16]; l_sdt = b_offset[20]; s_dp = b_offset[20]; s_mul = b_offset[20];
  //   b_offset[21] = a_mul; opc[3:0] = {IW_0[24], b_offset[23:22], a_mul}; w_sdt = a_mul; b_sdt = b_offset[22];
  //   opmul6[4:0] = {IW_0[27:26], i_dp, IW_0[24], b_offset[23]}; u_sdt = b_offset[23]; l_b = IW_0[24];
  //   p_sdt = IW_0[24]; i_sdt = i_dp; opb3[2:0] = {IW_0[27:26], i_dp}; op2[1:0] = IW_0[27:26];
  //   opmul2[1:0] = IW_0[27:26]

  // Notes on the sheet:
  //   DP
  //   MUL
  //   SDT
  //   B
  //   SP
  //   LR
  //   PC
endmodule
