// Digital circuit project07_single_cycle.dig as structural Verilog
module project07_single_cycle (
  input  CLK,
  input  CLR,
  input  [2:0] PROG,
  output DONE,
  output [31:0] R0
);

  wire a_mul, ALUsrcB, C, CLK_t, i_dp, MR, MW, N, RFW, RR1sel, V, WDsel, WRsel, Z;
  wire [1:0] EXTop, PCsel, RR0sel;
  wire [2:0] ALUop;
  wire [3:0] cond, multiplexer_2_out, multiplexer_3_out, multiplexer_4_out;
  wire [7:0] decode_ascii_1_i_0, decode_ascii_1_i_1, decode_ascii_1_i_2, decode_ascii_1_i_3;
  wire [23:0] b_offset;
  wire [27:24] iw;
  wire [31:0] add_1_s, add_2_s, alu_1_r, extension_unit_1_p3, multiplexer_1_out, multiplexer_5_out,
       multiplexer_6_out, multiplexer_7_out, r1, r2, r3, r4, r5, r6, r7, r8, r9, r10, r11, r12, r13, r14,
       r15, RAM_d, register_clr_32bits_1_q, register_file_clr_1_rd0, register_file_clr_1_rd1;

  and and_1 (CLK_t, CLK, ~DONE);  // And
  // Probe on {cond, iw[27:26], i_dp, iw[24], b_offset[23:22], a_mul, b_offset[20:0]}
  register_clr_32bits register_clr_32bits_1 (
    .D(multiplexer_1_out), .C(CLK_t), .en(1'b1), .Q(register_clr_32bits_1_q), .clr(CLR));
  Multiplexer #(.Selector_Bits(2), .Bits(32)) multiplexer_1 (
    .sel(PCsel), .in_0(add_1_s), .in_1(multiplexer_7_out), .in_2(register_file_clr_1_rd1), .in_3({32{1'b0}}),
    .out(multiplexer_1_out));
  // Probe on decode_ascii_1_i_0
  // Probe on decode_ascii_1_i_1
  decode_ascii decode_ascii_1 (
    .IW({cond, iw[27:26], i_dp, iw[24], b_offset[23:22], a_mul, b_offset[20:0]}), .I_0(decode_ascii_1_i_0),
    .I_1(decode_ascii_1_i_1), .I_2(decode_ascii_1_i_2), .I_3(decode_ascii_1_i_3));
  Add #(.Bits(32)) add_1 (.a(register_clr_32bits_1_q), .b(32'h4), .c_i(1'b0), .s(add_1_s));  // open: c_o
  // Probe on decode_ascii_1_i_2
  // Probe on decode_ascii_1_i_3
  instruction_memory instruction_memory_1 (
    .A(register_clr_32bits_1_q[8:2]), .PN(PROG),
    .D({cond, iw[27:26], i_dp, iw[24], b_offset[23:22], a_mul, b_offset[20:0]}));
  Add #(.Bits(32)) add_2 (.a(add_1_s), .b(32'h4), .c_i(1'b0), .s(add_2_s));  // open: c_o
  // Probe on R0
  // Probe on r1
  // Probe on r2
  // Probe on r3
  // Probe on cond
  // Probe on cond
  // Probe on cond
  // Probe on cond
  // Probe on r4
  // Probe on r5
  // Probe on r6
  // Probe on r7
  // Probe on iw[27:26]
  // Probe on {iw[27:26], i_dp, iw[24], b_offset[23]}
  // Probe on iw[27:26]
  // Probe on {iw[27:26], i_dp}
  // Probe on i_dp
  // Probe on i_dp
  // Probe on iw[24]
  decoder decoder_1 (
    .IW({cond, iw[27:26], i_dp, iw[24], b_offset[23:22], a_mul, b_offset[20:0]}), .RFW(RFW), .EXTop(EXTop),
    .ALUsrcB(ALUsrcB), .ALUop(ALUop), .PCsel(PCsel), .RR0sel(RR0sel), .RR1sel(RR1sel), .WRsel(WRsel),
    .WDsel(WDsel), .MR(MR), .MW(MW));
  // Probe on {iw[24], b_offset[23:22], a_mul}
  // Probe on a_mul
  // Probe on iw[24]
  // Probe on r8
  // Probe on r9
  // Probe on r10
  // Probe on r11
  // Probe on b_offset[20]
  // Probe on b_offset[23]
  // Probe on {b_offset[23:22], a_mul, b_offset[20:0]}
  Multiplexer #(.Selector_Bits(2), .Bits(4)) multiplexer_2 (
    .sel(RR0sel), .in_0(b_offset[19:16]), .in_1(4'b1111), .in_2(4'b0000), .in_3(4'b0000),
    .out(multiplexer_2_out));
  Multiplexer #(.Bits(4)) multiplexer_3 (
    .sel(RR1sel), .in_0(b_offset[3:0]), .in_1(b_offset[15:12]), .out(multiplexer_3_out));
  Multiplexer #(.Bits(4)) multiplexer_4 (.sel(WRsel), .in_0(b_offset[15:12]), .in_1(4'b1110), .out(multiplexer_4_out));
  Multiplexer #(.Bits(32)) multiplexer_5 (
    .sel(WDsel), .in_0(multiplexer_7_out), .in_1(add_1_s), .out(multiplexer_5_out));
  // Probe on b_offset[20]
  // Probe on b_offset[19:16]
  // Probe on b_offset[22]
  // Probe on b_offset[19:16]
  // Probe on b_offset[15:12]
  // Probe on a_mul
  // Probe on r12
  // Probe on r13
  // Probe on r14
  // Probe on r15
  // Probe on b_offset[15:12]
  // Probe on b_offset[11:8]
  // Probe on b_offset[20]
  register_file_clr register_file_clr_1 (
    .ReadReg0(multiplexer_2_out), .ReadReg1(multiplexer_3_out), .WriteReg(multiplexer_4_out),
    .WriteData(multiplexer_5_out), .WriteEn(RFW), .PC(add_2_s), .CLK(CLK_t), .RD0(register_file_clr_1_rd0),
    .RD1(register_file_clr_1_rd1), .r0(R0), .r1(r1), .r2(r2), .r3(r3), .r4(r4), .r5(r5), .r6(r6), .r7(r7),
    .r8(r8), .r9(r9), .r10(r10), .r11(r11), .r12(r12), .r13(r13), .r14(r14), .r15(r15), .CLR(CLR));
  // Probe on b_offset[3:0]
  // Probe on b_offset[7:0]
  // Probe on b_offset[19:16]
  // Probe on N
  // Probe on Z
  // Probe on C
  // Probe on V
  // Probe on b_offset[7:4]
  // Probe on b_offset[15:12]
  // Probe on b_offset[3:0]
  // Probe on b_offset[3:0]
  // Probe on b_offset[11:0]
  Multiplexer #(.Bits(32)) multiplexer_6 (
    .sel(ALUsrcB), .in_0(register_file_clr_1_rd1), .in_1(extension_unit_1_p3), .out(multiplexer_6_out));
  // extension_unit extension_unit_1: pin names not known; wires that end beside it: {cond, iw[27:26], i_dp, iw[24], b_offset[23:22], a_mul, b_offset[20:0]}, EXTop, extension_unit_1_p3
  alu alu_1 (
    .A(register_file_clr_1_rd0), .B(multiplexer_6_out), .R(alu_1_r), .N(N), .Z(Z), .C(C), .V(V), .ALUOp(ALUop));  // open: NZCV
  // Probe on extension_unit_1_p3
  Comparator #(.Bits(32)) comparator_1 (
    .a({cond, iw[27:26], i_dp, iw[24], b_offset[23:22], a_mul, b_offset[20:0]}), .b(32'he2800000), .eq(DONE));  // open: gt, lt
  Multiplexer #(.Bits(32)) multiplexer_7 (.sel(MR), .in_0(alu_1_r), .in_1(RAM_d), .out(multiplexer_7_out));
  RAMDualPort #(.AddrBits(8), .Bits(32)) RAM (
    .A(alu_1_r[9:2]), .Din(register_file_clr_1_rd1), .str(MW), .C(CLK_t), .ld(MR), .D(RAM_d));

  // Other names for the same wires on the sheet: imm[7:0] = b_offset[7:0]; immoff[11:0] = b_offset[11:0];
  //   iw (some bits) = {cond, i_dp, b_offset[23:22], a_mul, b_offset[20:0]}; rm[3:0] = b_offset[3:0];
  //   rm_mul[3:0] = b_offset[3:0]; opmul4[3:0] = b_offset[7:4]; rs_mul[3:0] = b_offset[11:8];
  //   rd[3:0] = b_offset[15:12]; rn_mul[3:0] = b_offset[15:12]; rd_mul[3:0] = b_offset[19:16];
  //   rn[3:0] = b_offset[19:16]; l_sdt = b_offset[20]; s_dp = b_offset[20]; s_mul = b_offset[20];
  //   b_offset[21] = a_mul; opc[3:0] = {iw[24], b_offset[23:22], a_mul}; w_sdt = a_mul; b_sdt = b_offset[22];
  //   opmul6[4:0] = {iw[27:26], i_dp, iw[24], b_offset[23]}; u_sdt = b_offset[23]; l_b = iw[24]; p_sdt = iw[24];
  //   i_sdt = i_dp; opb3[2:0] = {iw[27:26], i_dp}; op2[1:0] = iw[27:26]; opmul2[1:0] = iw[27:26]

  // Notes on the sheet:
  //   DP
  //   MUL
  //   SDT
  //   B
  //   SP
  //   LR
  //   PC
endmodule
