// Digital circuit register_file_clr.dig as structural Verilog
module register_file_clr (
  input  [3:0] ReadReg0,
  input  [3:0] ReadReg1,
  input  CLK,
  input  [3:0] WriteReg,
  input  [31:0] WriteData,
  input  [31:0] PC,
  input  WriteEn,
  input  CLR,
  output [31:0] RD0,
  output [31:0] RD1,
  output [31:0] r0,
  output [31:0] r1,
  output [31:0] r2,
  output [31:0] r3,
  output [31:0] r4,
  output [31:0] r5,
  output [31:0] r6,
  output [31:0] r7,
  output [31:0] r8,
  output [31:0] r9,
  output [31:0] r10,
  output [31:0] r11,
  output [31:0] r12,
  output [31:0] r13,
  output [31:0] r14,
  output [31:0] r15
);

  wire _4to16_decoder_with_enable_1_out_0, _4to16_decoder_with_enable_1_out_1,
       _4to16_decoder_with_enable_1_out_2, _4to16_decoder_with_enable_1_out_3,
       _4to16_decoder_with_enable_1_out_4, _4to16_decoder_with_enable_1_out_5,
       _4to16_decoder_with_enable_1_out_6, _4to16_decoder_with_enable_1_out_7,
       _4to16_decoder_with_enable_1_out_8, _4to16_decoder_with_enable_1_out_9,
       _4to16_decoder_with_enable_1_out_10, _4to16_decoder_with_enable_1_out_11,
       _4to16_decoder_with_enable_1_out_12, _4to16_decoder_with_enable_1_out_13,
       _4to16_decoder_with_enable_1_out_14;

  _4to16_decoder_with_enable _4to16_decoder_with_enable_1 (
    .Sel(WriteReg), .EN(WriteEn), .out_0(_4to16_decoder_with_enable_1_out_0),
    .out_1(_4to16_decoder_with_enable_1_out_1), .out_2(_4to16_decoder_with_enable_1_out_2),
    .out_3(_4to16_decoder_with_enable_1_out_3), .out_4(_4to16_decoder_with_enable_1_out_4),
    .out_5(_4to16_decoder_with_enable_1_out_5), .out_6(_4to16_decoder_with_enable_1_out_6),
    .out_7(_4to16_decoder_with_enable_1_out_7), .out_8(_4to16_decoder_with_enable_1_out_8),
    .out_9(_4to16_decoder_with_enable_1_out_9), .out_10(_4to16_decoder_with_enable_1_out_10),
    .out_11(_4to16_decoder_with_enable_1_out_11), .out_12(_4to16_decoder_with_enable_1_out_12),
    .out_13(_4to16_decoder_with_enable_1_out_13), .out_14(_4to16_decoder_with_enable_1_out_14));  // open: out_15
  register_clr_32bits register_clr_32bits_1 (
    .D(WriteData), .C(CLK), .en(_4to16_decoder_with_enable_1_out_0), .Q(r0), .clr(CLR));
  register_clr_32bits register_clr_32bits_2 (
    .D(WriteData), .C(CLK), .en(_4to16_decoder_with_enable_1_out_1), .Q(r1), .clr(CLR));
  register_clr_32bits register_clr_32bits_3 (
    .D(WriteData), .C(CLK), .en(_4to16_decoder_with_enable_1_out_2), .Q(r2), .clr(CLR));
  register_clr_32bits register_clr_32bits_4 (
    .D(WriteData), .C(CLK), .en(_4to16_decoder_with_enable_1_out_3), .Q(r3), .clr(CLR));
  register_clr_32bits register_clr_32bits_5 (
    .D(WriteData), .C(CLK), .en(_4to16_decoder_with_enable_1_out_4), .Q(r4), .clr(CLR));
  register_clr_32bits register_clr_32bits_6 (
    .D(WriteData), .C(CLK), .en(_4to16_decoder_with_enable_1_out_5), .Q(r5), .clr(CLR));
  register_clr_32bits register_clr_32bits_7 (
    .D(WriteData), .C(CLK), .en(_4to16_decoder_with_enable_1_out_6), .Q(r6), .clr(CLR));
  register_clr_32bits register_clr_32bits_8 (
    .D(WriteData), .C(CLK), .en(_4to16_decoder_with_enable_1_out_7), .Q(r7), .clr(CLR));
  register_clr_32bits register_clr_32bits_9 (
    .D(WriteData), .C(CLK), .en(_4to16_decoder_with_enable_1_out_8), .Q(r8), .clr(CLR));
  register_clr_32bits register_clr_32bits_10 (
    .D(WriteData), .C(CLK), .en(_4to16_decoder_with_enable_1_out_9), .Q(r9), .clr(CLR));
  register_clr_32bits register_clr_32bits_11 (
    .D(WriteData), .C(CLK), .en(_4to16_decoder_with_enable_1_out_10), .Q(r10), .clr(CLR));
  register_clr_32bits register_clr_32bits_12 (
    .D(WriteData), .C(CLK), .en(_4to16_decoder_with_enable_1_out_11), .Q(r11), .clr(CLR));
  register_clr_32bits register_clr_32bits_13 (
    .D(WriteData), .C(CLK), .en(_4to16_decoder_with_enable_1_out_12), .Q(r12), .clr(CLR));
  register_clr_32bits register_clr_32bits_14 (
    .D(WriteData), .C(CLK), .en(_4to16_decoder_with_enable_1_out_13), .Q(r13), .clr(CLR));
  register_clr_32bits register_clr_32bits_15 (
    .D(WriteData), .C(CLK), .en(_4to16_decoder_with_enable_1_out_14), .Q(r14), .clr(CLR));
  Multiplexer #(.Selector_Bits(4), .Bits(32)) multiplexer_1 (
    .sel(ReadReg1), .in_0(r0), .in_1(r1), .in_2(r2), .in_3(r3), .in_4(r4), .in_5(r5), .in_6(r6), .in_7(r7),
    .in_8(r8), .in_9(r9), .in_10(r10), .in_11(r11), .in_12(r12), .in_13(r13), .in_14(r14), .in_15(PC),
    .out(RD1));
  Multiplexer #(.Selector_Bits(4), .Bits(32)) multiplexer_2 (
    .sel(ReadReg0), .in_0(r0), .in_1(r1), .in_2(r2), .in_3(r3), .in_4(r4), .in_5(r5), .in_6(r6), .in_7(r7),
    .in_8(r8), .in_9(r9), .in_10(r10), .in_11(r11), .in_12(r12), .in_13(r13), .in_14(r14), .in_15(PC),
    .out(RD0));

  assign r15 = PC;
endmodule
