// Digital circuit register_clr_1bit.dig as structural Verilog
module register_clr_1bit (
  input  D,
  input  C,
  input  clr,
  input  en,
  output Q
);

  wire multiplexer_1_out, or_1_out;

  Multiplexer multiplexer_1 (.sel(clr), .in_0(D), .in_1(1'b0), .out(multiplexer_1_out));
  or or_1 (or_1_out, en, clr);
  Register register_1 (.D(multiplexer_1_out), .C(C), .en(or_1_out), .Q(Q));
endmodule
