// Digital circuit register_clr_2bits.dig as structural Verilog
module register_clr_2bits (
  input  [1:0] D,
  input  C,
  input  clr,
  input  en,
  output [1:0] Q
);

  wire or_1_out;
  wire [1:0] multiplexer_1_out;

  Multiplexer #(.Bits(2)) multiplexer_1 (.sel(clr), .in_0(D), .in_1(2'b00), .out(multiplexer_1_out));
  or or_1 (or_1_out, en, clr);
  Register #(.Bits(2)) register_1 (.D(multiplexer_1_out), .C(C), .en(or_1_out), .Q(Q));
endmodule
