// Digital circuit register_clr_3bits.dig as structural Verilog
module register_clr_3bits (
  input  [2:0] D,
  input  C,
  input  clr,
  input  en,
  output [2:0] Q
);

  wire or_1_out;
  wire [2:0] multiplexer_1_out;

  Multiplexer #(.Bits(3)) multiplexer_1 (.sel(clr), .in_0(D), .in_1(3'b000), .out(multiplexer_1_out));
  or or_1 (or_1_out, en, clr);
  Register #(.Bits(3)) register_1 (.D(multiplexer_1_out), .C(C), .en(or_1_out), .Q(Q));
endmodule
