// Digital circuit register_clr_4bits.dig as structural Verilog
module register_clr_4bits (
  input  [3:0] D,
  input  C,
  input  clr,
  input  en,
  output [3:0] Q
);

  wire or_1_out;
  wire [3:0] multiplexer_1_out;

  Multiplexer #(.Bits(4)) multiplexer_1 (.sel(clr), .in_0(D), .in_1(4'b0000), .out(multiplexer_1_out));
  or or_1 (or_1_out, en, clr);
  Register #(.Bits(4)) register_1 (.D(multiplexer_1_out), .C(C), .en(or_1_out), .Q(Q));
endmodule
